// Logisim project 4bit_sub.circ as structural Verilog
module fourBitNeg (
  input  x0,
  input  x1,
  input  x2,
  input  x3,
  output out0,
  output out1,
  output out2,
  output out3
);

  wire adder_1_cout, adder_2_cout, adder_3_cout, not_1_out, not_2_out, not_3_out, not_4_out;

  not not_1 (not_1_out, x0);
  Adder #(.width(1)) adder_1 (.a(not_1_out), .b(1'b0), .out(out0), .cin(1'b1), .cout(adder_1_cout));
  not not_2 (not_2_out, x1);
  Adder #(.width(1)) adder_2 (.a(not_2_out), .b(1'b0), .out(out1), .cin(adder_1_cout), .cout(adder_2_cout));
  not not_3 (not_3_out, x2);
  Adder #(.width(1)) adder_3 (.a(not_3_out), .b(1'b0), .out(out2), .cin(adder_2_cout), .cout(adder_3_cout));
  not not_4 (not_4_out, x3);
  Adder #(.width(1)) adder_4 (.a(not_4_out), .b(1'b0), .out(out3), .cin(adder_3_cout));  // open: cout
endmodule

module fourBitSubtractor (
  input  [3:0] b,
  input  [3:0] a,
  output [3:0] c
);

  wire [3:0] fourbitneg_1_out0;

  Adder #(.width(4)) adder_1 (.a(a), .b(fourbitneg_1_out0), .out(c), .cin(1'b0));  // open: cout
  fourBitNeg fourbitneg_1 (
    .x0(b[0]), .x1(b[1]), .x2(b[2]), .x3(b[3]), .out0(fourbitneg_1_out0[0]), .out1(fourbitneg_1_out0[1]),
    .out2(fourbitneg_1_out0[2]), .out3(fourbitneg_1_out0[3]));
endmodule

module fourBitComparator (
  input  [3:0] b,
  input  [3:0] a,
  output out_3
);

  wire [3:0] fourbitsubtractor_1_c;

  fourBitSubtractor fourbitsubtractor_1 (.b(b), .a(a), .c(fourbitsubtractor_1_c));
  nor nor_1 (out_3, fourbitsubtractor_1_c[0], fourbitsubtractor_1_c[1], fourbitsubtractor_1_c[2], fourbitsubtractor_1_c[3]);
endmodule
