// Logisim project HW0_P2_3bitEncoder.circ as structural Verilog: 1 circuit, main circuit main
module main (
  input  in_1,
  input  in_2,
  input  in_3,
  input  in_4,
  input  in_5,
  input  in_6,
  output O
);

  // NOT_Gate not_1 has open pins: in=in_1, out=open
  // NOT_Gate not_2 has open pins: in=in_4, out=open
  // NOT_Gate not_3 has open pins: in=in_2, out=open
  // NOT_Gate not_4 has open pins: in=in_3, out=open
  // NOT_Gate not_5 has open pins: in=in_5, out=open
  // NOT_Gate not_6 has open pins: in=in_6, out=open
  // OR_Gate or_1 has open pins: out=O
endmodule
