// Logisim project HW1_ALU.circ as structural Verilog: 6 circuits, main circuit main
module main (
  input  [3:0] X,
  input  [3:0] Y,
  input  zx,
  input  zy,
  input  nx,
  input  ny,
  input  f,
  input  no,
  output [3:0] oout
);

  wire [3:0] adder_1_out, and_1_out, multiplexer_1_out, multiplexer_2_out, multiplexer_3_out,
       multiplexer_4_out, multiplexer_5_out, not_1_out, not_2_out, not_3_out;

  Hex_Digit_Display hex_digit_display_1 (.value(X));  // open: dp
  Multiplexer #(.width(4)) multiplexer_1 (.in0(X), .in1(4'b0000), .out(multiplexer_1_out), .sel(zx));
  assign not_1_out = ~multiplexer_1_out;  // NOT_Gate not_1, 4 bits wide
  Multiplexer #(.width(4)) multiplexer_2 (.in0(multiplexer_1_out), .in1(not_1_out), .out(multiplexer_2_out), .sel(nx));
  Adder #(.width(4)) adder_1 (
    .a(multiplexer_4_out), .b(multiplexer_2_out), .out(adder_1_out), .cin(1'b0));  // open: cout
  Hex_Digit_Display hex_digit_display_2 (.value(Y));  // open: dp
  Multiplexer #(.width(4)) multiplexer_3 (.in0(Y), .in1(4'b0000), .out(multiplexer_3_out), .sel(zy));
  assign not_2_out = ~multiplexer_3_out;  // NOT_Gate not_2, 4 bits wide
  Multiplexer #(.width(4)) multiplexer_4 (.in0(multiplexer_3_out), .in1(not_2_out), .out(multiplexer_4_out), .sel(ny));
  assign and_1_out = multiplexer_2_out & multiplexer_4_out;  // AND_Gate and_1, 4 bits wide
  Multiplexer #(.width(4)) multiplexer_5 (.in0(adder_1_out), .in1(and_1_out), .out(multiplexer_5_out), .sel(f));
  assign not_3_out = ~multiplexer_5_out;  // NOT_Gate not_3, 4 bits wide
  Multiplexer #(.width(4)) multiplexer_6 (.in0(multiplexer_5_out), .in1(not_3_out), .out(oout), .sel(no));
  Hex_Digit_Display hex_digit_display_3 (.value(oout));  // open: dp

  // Notes on the sheet:
  //   Jackson Darling
  //   CSCI 221
endmodule

module fourBitNeg (
  input  [3:0] x,
  output [3:0] xout
);

  wire adder_1_cout, adder_2_cout, adder_3_cout;
  wire [3:0] not_1_out;

  assign not_1_out = ~x;  // NOT_Gate not_1, 4 bits wide
  Adder #(.width(1)) adder_1 (.a(not_1_out[0]), .b(1'b0), .out(xout[0]), .cin(1'b1), .cout(adder_1_cout));
  Adder #(.width(1)) adder_2 (.a(not_1_out[1]), .b(1'b0), .out(xout[1]), .cin(adder_1_cout), .cout(adder_2_cout));
  Adder #(.width(1)) adder_3 (.a(not_1_out[2]), .b(1'b0), .out(xout[2]), .cin(adder_2_cout), .cout(adder_3_cout));
  Adder #(.width(1)) adder_4 (.a(not_1_out[3]), .b(1'b0), .out(xout[3]), .cin(adder_3_cout));  // open: cout
endmodule

module fourBitSubtractor (
  input  [3:0] b,
  input  [3:0] a,
  output [3:0] c
);

  wire [3:0] fourbitneg_1_xout;

  fourBitNeg fourbitneg_1 (.x(b), .xout(fourbitneg_1_xout));
  Adder #(.width(4)) adder_1 (.a(a), .b(fourbitneg_1_xout), .out(c), .cin(1'b0));  // open: cout
endmodule

module fourBitComparator (
  input  [3:0] b,
  input  [3:0] a,
  output out_3
);

  wire [3:0] fourbitsubtractor_1_c;

  fourBitSubtractor fourbitsubtractor_1 (.b(b), .a(a), .c(fourbitsubtractor_1_c));
  nor nor_1 (out_3, fourbitsubtractor_1_c[0], fourbitsubtractor_1_c[1], fourbitsubtractor_1_c[2], fourbitsubtractor_1_c[3]);
endmodule

module bitlfip (
  input  [3:0] in_1,
  output [3:0] out_2
);

  assign out_2 = ~in_1;  // NOT_Gate not_1, 4 bits wide
endmodule

module bitwiseAnd (
  input  [3:0] b,
  input  [3:0] a,
  output [3:0] out_3
);

  assign out_3 = b & a;  // AND_Gate and_1, 4 bits wide
endmodule
