// Logisim project sm_evolution.circ as structural Verilog: 3 circuits, main circuit main
module main (
  input  \input ,
  input  clear,
  output just_saw_101
);

  wire clock_1_out;
  wire [1:0] neext_s0_out, register_1_q;

  next neext (
    .\input (\input ), .s1(register_1_q[1]), .s0(register_1_q[0]), .s1_out(neext_s0_out[1]),
    .s0_out(neext_s0_out[0]));
  Clock clock_1 (.out(clock_1_out));
  Register #(.width(2)) register_1 (.D(neext_s0_out), .en(1'b1), .Q(register_1_q), .clk(clock_1_out), .clr(clear));
  out oout (.s1(register_1_q[1]), .s0(register_1_q[0]), .\output (just_saw_101));

  // Notes on the sheet:
  //   Jackson Darling
  //   2/14/22
  //   CSCI 221
endmodule

module next (
  input  \input ,
  input  s1,
  input  s0,
  output s1_out,
  output s0_out
);

  wire and_1_out, and_2_out, and_3_out, not_1_out, not_2_out, not_3_out;

  not not_1 (not_1_out, \input );
  not not_2 (not_2_out, s1);
  not not_3 (not_3_out, s0);
  and and_1 (and_1_out, not_2_out, not_3_out, \input );
  and and_2 (and_2_out, s1, not_3_out, not_1_out);
  and and_3 (and_3_out, not_2_out, s0, \input );
  or or_1 (s1_out, and_1_out, and_3_out);
  or or_2 (s0_out, and_2_out, and_3_out);
endmodule

module out (
  input  s1,
  input  s0,
  output \output 
);

  and and_1 (\output , s1, s0);
endmodule
