// Logisim project mux4.circ as structural Verilog: 1 circuit, main circuit main
module main (
  input  Select0,
  input  Select1,
  input  line00,
  input  line01,
  input  line10,
  input  line11,
  output O
);

  wire four_out, not_1_out, not_2_out, one_out, three_out, two_out;

  and one (one_out, line00, not_2_out, not_1_out);
  and two (two_out, line01, Select1, not_1_out);
  or or_1 (O, one_out, two_out, three_out, four_out);
  not not_1 (not_1_out, Select0);
  not not_2 (not_2_out, Select1);
  and three (three_out, line10, not_2_out, Select0);
  and four (four_out, Select1, Select0, line11);

  // Notes on the sheet:
  //   CSCI 221
  //   Jackson Darling
  //   HW1 - P2 - mux4
endmodule
