// Logisim project 4bit_neg.circ as structural Verilog
module main (
  input  x0,
  input  x1,
  input  x2,
  input  x3,
  output out0,
  output out1,
  output out2,
  output out3
);

  wire adder_1_cout, adder_2_cout, adder_3_cout, not_1_out, not_2_out, not_3_out, not_4_out;

  not not_1 (not_1_out, x0);
  Adder #(.width(1)) adder_1 (.a(not_1_out), .b(1'b0), .out(out0), .cin(1'b1), .cout(adder_1_cout));
  not not_2 (not_2_out, x1);
  Adder #(.width(1)) adder_2 (.a(not_2_out), .b(1'b0), .out(out1), .cin(adder_1_cout), .cout(adder_2_cout));
  not not_3 (not_3_out, x2);
  Adder #(.width(1)) adder_3 (.a(not_3_out), .b(1'b0), .out(out2), .cin(adder_2_cout), .cout(adder_3_cout));
  not not_4 (not_4_out, x3);
  Adder #(.width(1)) adder_4 (.a(not_4_out), .b(1'b0), .out(out3), .cin(adder_3_cout));  // open: cout
endmodule
