// Logisim project minimizeme.circ as structural Verilog: 2 circuits, main circuit main
module main (
  input  A,
  input  B,
  input  C,
  input  D,
  output out_5
);

  wire and_1_out, and_2_out, and_3_out, and_4_out, and_5_out, and_6_out, not_1_out, not_2_out, not_3_out,
       not_4_out;

  not not_1 (not_1_out, A);
  not not_2 (not_2_out, B);
  not not_3 (not_3_out, C);
  not not_4 (not_4_out, D);
  and and_1 (and_1_out, not_1_out, B, not_3_out, D);
  and and_2 (and_2_out, not_1_out, B, C, not_4_out);
  and and_3 (and_3_out, not_1_out, B, not_3_out, not_4_out);
  and and_4 (and_4_out, not_1_out, not_2_out, C, not_4_out);
  and and_5 (and_5_out, A, B, not_3_out, D);
  and and_6 (and_6_out, not_1_out, B, not_3_out, not_4_out);
  or or_1 (out_5, and_1_out, and_2_out, and_3_out, and_4_out, and_5_out, and_6_out);
endmodule

module Minimized (
  input  a,
  input  b,
  input  c,
  input  d,
  output oout
);

  wire and_1_out, and_2_out, and_3_out, not_1_out, not_2_out, not_3_out, not_4_out;

  not not_1 (not_1_out, a);
  not not_2 (not_2_out, b);
  not not_3 (not_3_out, c);
  not not_4 (not_4_out, d);
  and and_1 (and_1_out, not_1_out, c, not_4_out);
  and and_2 (and_2_out, not_1_out, b, not_3_out);
  and and_3 (and_3_out, b, not_3_out, d);
  or or_1 (oout, and_1_out, and_2_out, and_3_out);
endmodule
