// Logisim project majorityOfThree.circ as structural Verilog: 1 circuit, main circuit main
module main (
  input  X,
  input  Y,
  input  Z,
  output O
);

  wire and_1_out, and_2_out, and_3_out, and_4_out, not_1_out, not_2_out, not_3_out;

  not not_1 (not_1_out, X);
  not not_2 (not_2_out, Y);
  not not_3 (not_3_out, Z);
  and and_1 (and_1_out, X, Y, Z);
  and and_2 (and_2_out, X, Y, not_3_out);
  and and_3 (and_3_out, X, not_2_out, Z);
  and and_4 (and_4_out, not_1_out, Y, Z);
  or or_1 (O, and_1_out, and_2_out, and_3_out, and_4_out);
endmodule
