// Logisim project HW0_P1_2bitEncoder.circ as structural Verilog: 1 circuit, main circuit main
module main (
  input  C1,
  input  C2,
  output D11,
  output D10,
  output D01,
  output D00
);

  wire not_1_out, not_2_out;

  not not_1 (not_1_out, C1);
  not not_2 (not_2_out, C2);
  and and_1 (D11, C2, C1);
  and and_2 (D10, C1, not_2_out);
  and and_3 (D01, not_1_out, C2);
  and and_4 (D00, not_2_out, not_1_out);
endmodule
