// Logisim project HW0_P2_3bitEncoder.circ as structural Verilog: 1 circuit, main circuit main
module main (
  input  x0,
  input  y0,
  input  x1,
  input  y1,
  input  x2,
  input  y2,
  output out_7
);

  wire and_1_out, and_2_out, and_3_out, and_4_out, and_5_out, and_6_out, not_1_out, not_2_out, not_3_out,
       not_4_out, not_5_out, not_6_out, or_1_out;

  not not_1 (not_1_out, x0);
  not not_2 (not_2_out, x1);
  not not_3 (not_3_out, x2);
  and and_1 (and_1_out, not_3_out, not_2_out, not_1_out);
  and and_2 (and_2_out, not_3_out, and_4_out);
  and and_3 (and_3_out, y2, x2);
  not not_4 (not_4_out, y0);
  not not_5 (not_5_out, y1);
  and and_4 (and_4_out, not_4_out, not_5_out, not_6_out);
  and and_5 (and_5_out, not_6_out, and_1_out);
  or or_1 (or_1_out, and_2_out, and_5_out);
  or or_2 (out_7, and_3_out, and_6_out, or_1_out);
  not not_6 (not_6_out, y2);
  and and_6 (and_6_out, not_3_out, not_6_out);

  // Notes on the sheet:
  //   Jackson Darling
  //   CSCI 221
  //   HW0 - P2 - 3bitEncoder
endmodule
