// Logisim project HW0_P3.circ as structural Verilog: 1 circuit, main circuit main
module main (
  input  A,
  input  B,
  input  C,
  input  D,
  output out_5
);

  wire and_1_out, and_2_out, and_3_out, and_4_out, and_5_out, and_6_out, and_7_out, and_8_out, not_1_out,
       not_2_out, not_3_out, not_4_out;

  not not_1 (not_1_out, A);
  not not_2 (not_2_out, B);
  not not_3 (not_3_out, C);
  not not_4 (not_4_out, D);
  and and_1 (and_1_out, not_1_out, not_2_out, not_3_out, D);
  and and_2 (and_2_out, not_1_out, not_2_out, C, not_4_out);
  and and_3 (and_3_out, not_1_out, B, not_3_out, not_4_out);
  and and_4 (and_4_out, not_1_out, B, C, D);
  and and_5 (and_5_out, A, B, not_3_out, D);
  and and_6 (and_6_out, A, not_2_out, not_3_out, not_4_out);
  and and_7 (and_7_out, A, B, C, not_4_out);
  and and_8 (and_8_out, D, C, not_2_out, A);
  or or_1 (out_5, and_7_out, and_3_out, and_1_out, and_2_out, and_4_out, and_5_out, and_6_out, and_8_out);

  // Notes on the sheet:
  //   CSCI 121
  //   HW0 - P3 
  //   Jackson Darling
endmodule
