// Logisim project counter2-evolution.circ as structural Verilog: 3 circuits, main circuit main
module main (
  input  down_3ad2e347,
  input  clear
);

  wire clock_1_out, out_1_bot, out_1_lbot, out_1_ltop, out_1_out_6, out_1_rbot, out_1_rtop, out_1_top;
  wire [1:0] next_1_q0_271472b8, register_1_q;

  Register #(.width(2)) register_1 (
    .D(next_1_q0_271472b8), .en(1'b1), .clk(clock_1_out), .Q(register_1_q), .clr(clear));
  next next_1 (
    .d(down_3ad2e347), .q1(register_1_q[1]), .q0(register_1_q[0]), .q1_481816aa(next_1_q0_271472b8[1]),
    .q0_271472b8(next_1_q0_271472b8[0]));
  Clock clock_1 (.out(clock_1_out));
  out out_1 (
    .q1(register_1_q[1]), .q0(register_1_q[0]), .top(out_1_top), .ltop(out_1_ltop), .rtop(out_1_rtop),
    .out_6(out_1_out_6), .lbot(out_1_lbot), .rbot(out_1_rbot), .bot(out_1_bot));
  next next_2 ();  // open: d, q1, q0, q1_481816aa, q0_271472b8
  _7_Segment_Display u_7_segment_display_1 (
    .g(out_1_out_6), .f(out_1_ltop), .a(out_1_top), .b(out_1_rtop), .e(out_1_lbot), .d(out_1_bot),
    .c(out_1_rbot));  // open: dp
endmodule

module next (
  input  d,
  input  q1,
  input  q0,
  output q1_481816aa,
  output q0_271472b8
);

  // NOT_Gate not_1 has open pins: in=d, out=open
  xor xor_1 (q1_481816aa, q1, q0);
  not not_2 (q0_271472b8, q0);
endmodule

module out (
  input  q1,
  input  q0,
  output top,
  output ltop,
  output rtop,
  output out_6,
  output lbot,
  output rbot,
  output bot
);

  wire and_2_out, and_3_out, not_1_out, not_2_out, not_3_out, not_4_out;

  not not_1 (not_1_out, q1);
  not not_2 (not_2_out, q0);
  not not_3 (not_3_out, q1);
  not not_4 (not_4_out, q0);
  and and_1 (ltop, not_1_out, not_2_out);
  and and_2 (and_2_out, not_3_out, q0);
  not not_5 (bot, and_2_out);
  not not_6 (lbot, q0);
  and and_3 (and_3_out, q1, not_4_out);
  not not_7 (rbot, and_3_out);

  assign out_6 = q1;
  assign rtop = 1'b1;
  assign top = bot;
endmodule
